# Fritzing sketch Iot_code_challenge_May2018 (saved by Fritzing 0.9.3b)
breadboards: 1

parts:
  R1 = Resistor [tolerance=±5% resistance=220 package=THT]  # not connected
  Raspberry_Pi_1 = Raspberry Pi 3 [part_number=RPI-3-V1.2]
  RHT1 = Humidity and Temperature Sensor RHT03
  R2 = Resistor [tolerance=±5% resistance=1k package=THT]
  LED1 = LED - 5mm [color="Red (633nm)" package="5 mm [THT]"]

nets:
  N1: Raspberry_Pi_1.GIPO4, RHT1.Data-signal
  N2: Raspberry_Pi_1.GND, RHT1.GND_2, R2.Pin_0, LED1.cathode
  5V: Raspberry_Pi_1.5V, RHT1.Vcc
  N3: R2.Pin_1, LED1.anode
